// Logisim project Circuit 1. Latch.circ as structural Verilog: 1 circuit, main circuit main
module main (
  input  R,
  input  S,
  input  I,
  output Q,
  output not_Q,
  output O
);

  not nor_1 (Q, not_Q);  // NOR_Gate
  not nor_2 (not_Q, Q);  // NOR_Gate
  // Buffer buffer_1 has open pins: in=open, out=O
endmodule
