// Logisim project Circuit 2. Flip Flop.circ as structural Verilog: 1 circuit, main circuit main
module main (
  input  J,
  input  K,
  output Q
);

  wire clock_1_out;

  Clock clock_1 (.out(clock_1_out));
  J_K_Flip_Flop j_k_ff_1 (.J(J), .K(K), .clk(clock_1_out), .Q(Q));  // open: Qn, preset, reset
endmodule
