// Logisim project Circuit 5. Half Adder.circ as structural Verilog: 1 circuit, main circuit main
module main (
  input  A,
  input  B,
  output C,
  output S
);

  and and_1 (C, A, B);
  xor xor_1 (S, A, B);

  // Notes on the sheet:
  //   21101395 권준혁
  //   Truth Table
  //   A   B   |   C   S
  //   0   0   |   0   0
  //   0   1   |   0   1
  //   1   0   |   0   1
  //   1   1   |   1   0
endmodule
