// Logisim project Circuit 7. 7 Segment Decoder.circ as structural Verilog: 1 circuit, main circuit main
module main (
  input  in_1,
  input  in_2,
  input  in_3,
  input  in_4
);

  wire [6:0] plarom_1_p2;

  // PlaRom #(.Contents("0 0 2 0 2 0*4 2 0 2 0 1 0 1 0*5 1 0 0 2 0*5 2 2 0 0 1 1 0*7 2 0 0 1 0 0 2 0 0 2 0*9 2 1 0 2 1 2 0 1 0 1 0 1 2 0*7 2 1 0 1 0 1 0*4 2 0*5 1 1 0 2 0 1 0 2 1 0*5 2 0*5 2 1 0 2 1 0 0 1 2 0 1 0*6 1 0*6 1 0*6 1 0*14 1 0*6 1 0*6 1 0*6 1 0*14 1 0*6 1 0*6 1 0*6 1 0*14 1 0*6 1 0*6 1 0*6 1 0*14 1 0*6 1 0*14 1 0*6 1 0*6 1 0*6 1 0*14 1 0*6 1 0*6 1 0*6 1"), .\and (32), .outputs(7)) plarom_1: pin names not known; wires that end beside it: {in_1, in_2, in_3, in_4}, plarom_1_p2
  _7_Segment_Display u_7_segment_display_1 (
    .g(plarom_1_p2[0]), .f(plarom_1_p2[1]), .a(plarom_1_p2[6]), .b(plarom_1_p2[5]), .e(plarom_1_p2[2]),
    .d(plarom_1_p2[3]), .c(plarom_1_p2[4]));  // open: dp
endmodule
