// Logisim project Circuit 8. Programmable Logic Arrays.circ as structural Verilog: 1 circuit, main circuit main
module main (
  input  A,
  input  B,
  input  C_in
);

  wire [1:0] plarom_1_p2;

  // PlaRom #(.Contents("2 2 0 2 0 2 0 2 2 0*3 1 1 2 1 2 1 2 1 1 2*3 1 0 1 0 1 0*4 1 0 1 0 1 0 1"), .\and (8), .outputs(2)) plarom_1: pin names not known; wires that end beside it: {C_in, B, A}, plarom_1_p2
  LED led_1 (.in(plarom_1_p2[1]));
  LED led_2 (.in(plarom_1_p2[0]));

  // Notes on the sheet:
  //   Full_Adder
  //   C_out
  //   S
endmodule
