// Logisim project The Enigma Machine.circ as structural Verilog: 1 circuit, main circuit main
module main (
  input  [4:0] in_1,
  input  in_2,
  input  in_3,
  input  in_4,
  input  in_5,
  input  [6:0] in_6,
  input  in_7,
  input  in_8,
  input  [6:0] in_9,
  input  [4:0] in_10,
  input  in_11,
  input  in_12,
  input  in_13,
  input  in_14,
  input  [6:0] in_15,
  input  in_16,
  input  in_17,
  input  [6:0] in_18,
  input  [4:0] in_19,
  input  in_20,
  input  in_21,
  input  in_22,
  input  in_23,
  input  [6:0] in_24,
  input  in_25,
  input  in_26,
  input  [6:0] in_27,
  output [4:0] out_28,
  output [4:0] out_29,
  output [4:0] out_30,
  output [4:0] out_31,
  output [4:0] out_32,
  output [4:0] out_33
);

  wire A, a_t, and_1_out, and_2_out, and_3_out, and_4_out, and_5_out, and_6_out, B, b_t, C, c_t,
       comparator_1_lt, comparator_2_lt, comparator_3_lt, comparator_4_lt, comparator_5_lt, comparator_6_lt,
       D, d_t, E, e_t, F, f_t, G, g_t, H, h_t, I, i_t, J, j_t, K, k_t, L, l_t, M, m_t, N, n_t, not_1_out,
       not_2_out, not_3_out, not_4_out, not_5_out, not_6_out, not_7_out, not_8_out, not_9_out, not_10_out,
       not_11_out, not_12_out, O, o_t, P, p_t, pla_4_out, priority_encoder_1_p19, Q, q_t, R, r_t, S, s_t, T,
       t_t, U, u_t, V, v_t, W, w_t, X, x_t, Y, y_t, Z, z_t;
  wire [4:0] adder_4_out, adder_5_out, adder_6_out, bit_extender_7_out, bit_extender_8_out,
       bit_extender_9_out, counter_1_q, counter_2_q, counter_3_q, counter_4_q, counter_5_q, counter_6_q,
       multiplexer_4_out, pla_5_out, pla_6_out, pla_7_out, priority_encoder_1_p17, subtractor_4_out,
       subtractor_5_out, subtractor_6_out;
  wire [6:0] adder_1_out, adder_2_out, adder_3_out, bit_extender_1_out, bit_extender_2_out,
       bit_extender_3_out, bit_extender_4_out, bit_extender_5_out, bit_extender_6_out, multiplexer_1_out,
       multiplexer_2_out, multiplexer_3_out, subtractor_1_out, subtractor_2_out, subtractor_3_out;

  Counter #(.max('h1f), .width(5)) counter_1 (
    .clr(and_1_out), .load(in_2), .up(in_4), .count(in_7), .clk(priority_encoder_1_p19), .Q(counter_1_q));  // open: D, carry
  Counter #(.max('h1f), .width(5)) counter_2 (
    .clr(and_2_out), .load(in_11), .up(in_13), .count(in_16), .clk(and_1_out), .Q(counter_2_q));  // open: D, carry
  Counter #(.max('h1f), .width(5)) counter_3 (
    .clr(and_3_out), .load(in_20), .up(in_22), .count(in_25), .clk(and_2_out), .Q(counter_3_q));  // open: D, carry
  Button u_q (.out(q_t));
  not not_1 (not_1_out, counter_1_q[0]);
  and and_1 (and_1_out, not_1_out, counter_1_q[1], not_2_out, counter_1_q[3], counter_1_q[4]);
  not not_2 (not_2_out, counter_1_q[2]);
  not not_3 (not_3_out, counter_2_q[0]);
  and and_2 (and_2_out, not_3_out, counter_2_q[1], not_4_out, counter_2_q[3], counter_2_q[4]);
  not not_4 (not_4_out, counter_2_q[2]);
  not not_5 (not_5_out, counter_3_q[0]);
  and and_3 (and_3_out, not_5_out, counter_3_q[1], not_6_out, counter_3_q[3], counter_3_q[4]);
  not not_6 (not_6_out, counter_3_q[2]);
  Button u_w (.out(w_t));
  Button u_a (.out(a_t));
  Button u_s (.out(s_t));
  Button u_z (.out(z_t));
  Button u_e (.out(e_t));
  Button u_r (.out(r_t));
  Button u_d (.out(d_t));
  Button u_x (.out(x_t));
  Button u_t (.out(t_t));
  Button u_f (.out(f_t));
  Button u_c (.out(c_t));
  Button u_v (.out(v_t));
  assign bit_extender_1_out = {{2{1'b0}}, priority_encoder_1_p17};  // Bit_Extender bit_extender_1
  Adder #(.width(7)) adder_1 (.a(bit_extender_1_out), .b(bit_extender_2_out), .out(adder_1_out));  // open: cin, cout
  assign bit_extender_2_out = {{2{1'b0}}, counter_1_q};  // Bit_Extender bit_extender_2
  assign bit_extender_3_out = {{2{1'b0}}, out_28};  // Bit_Extender bit_extender_3
  Adder #(.width(7)) adder_2 (.a(bit_extender_3_out), .b(bit_extender_4_out), .out(adder_2_out));  // open: cin, cout
  assign bit_extender_4_out = {{2{1'b0}}, counter_2_q};  // Bit_Extender bit_extender_4
  assign bit_extender_5_out = {{2{1'b0}}, out_30};  // Bit_Extender bit_extender_5
  Adder #(.width(7)) adder_3 (.a(bit_extender_5_out), .b(bit_extender_6_out), .out(adder_3_out));  // open: cin, cout
  assign bit_extender_6_out = {{2{1'b0}}, counter_3_q};  // Bit_Extender bit_extender_6
  Button u_y (.out(y_t));
  Button u_g (.out(g_t));
  Button u_h (.out(h_t));
  Button u_b (.out(b_t));
  // Priority_Encoder #(.select(5)) priority_encoder_1: pin names not known; wires that end beside it: a_t, b_t, c_t, d_t, e_t, f_t, g_t, h_t, i_t, j_t, k_t, l_t, m_t, n_t, o_t, p_t, priority_encoder_1_p17, q_t, priority_encoder_1_p19, r_t, s_t, t_t, u_t, v_t, w_t, x_t, y_t, z_t
  Button u_u (.out(u_t));
  Button u_i (.out(i_t));
  Button u_j (.out(j_t));
  Button u_n (.out(n_t));
  Subtractor #(.width(7)) subtractor_1 (.a(adder_1_out), .b(in_6), .out(subtractor_1_out));  // open: bin, bout
  Comparator #(.mode("unsigned"), .width(7)) comparator_1 (
    .a(in_9), .b(adder_1_out), .lt(comparator_1_lt));  // open: gt, eq
  Subtractor #(.width(7)) subtractor_2 (.a(adder_2_out), .b(in_15), .out(subtractor_2_out));  // open: bin, bout
  Comparator #(.mode("unsigned"), .width(7)) comparator_2 (
    .a(in_18), .b(adder_2_out), .lt(comparator_2_lt));  // open: gt, eq
  Subtractor #(.width(7)) subtractor_3 (.a(adder_3_out), .b(in_24), .out(subtractor_3_out));  // open: bin, bout
  Comparator #(.mode("unsigned"), .width(7)) comparator_3 (
    .a(in_27), .b(adder_3_out), .lt(comparator_3_lt));  // open: gt, eq
  Button u_o (.out(o_t));
  Button u_k (.out(k_t));
  Button u_m (.out(m_t));
  Multiplexer #(.width(7)) multiplexer_1 (
    .in0(adder_1_out), .in1(subtractor_1_out), .out(multiplexer_1_out), .sel(comparator_1_lt));
  Multiplexer #(.width(7)) multiplexer_2 (
    .in0(adder_2_out), .in1(subtractor_2_out), .out(multiplexer_2_out), .sel(comparator_2_lt));
  Multiplexer #(.width(7)) multiplexer_3 (
    .in0(adder_3_out), .in1(subtractor_3_out), .out(multiplexer_3_out), .sel(comparator_3_lt));
  Button u_p (.out(p_t));
  Button u_l (.out(l_t));
  Bit_Extender #(.in_width(7), .out_width(5), .\type ("zero")) bit_extender_7 (
    .in(multiplexer_1_out), .out(bit_extender_7_out));
  PLA #(.in_width(5), .out_width(5), .\table ("00000 00001 # a-b\n00001 00000 # b-a\n00010 00011 # c-d\n00011 00010 # d-c\n00100 00101 # e-f\n00101 00100 # f-e\n00110 00111 # g-h\n00111 00110 # h-g\n01000 01001 # i-j\n01001 01000 # j-i\n01010 01011 # k-l\n01011 01010 # l-k\n01100 01101 # m-n\n01101 01100 # n-m\n01110 01111 # o-p\n01111 01110 # p-o\n10000 10001 # q-r\n10001 10000 # r-q\n10010 10011 # s-t\n10011 10010 # t-s\n10100 10101 # u-v\n10101 10100 # v-u\n10110 10111 # w-x\n10111 10110 # x-w\n11000 11001 # y-z\n11001 11000 # z-y")) pla_1 (
    .in(bit_extender_7_out), .out(out_28));
  Bit_Extender #(.in_width(7), .out_width(5), .\type ("zero")) bit_extender_8 (
    .in(multiplexer_2_out), .out(bit_extender_8_out));
  PLA #(.in_width(5), .out_width(5), .\table ("00000 11001 # a-z\n00001 11000 # b-y\n00010 10111 # c-x\n00011 10110 # d-w\n00100 10101 # e-v\n00101 10100 # f-u\n00110 10011 # g-t\n00111 10010 # h-s\n01000 10001 # i-r\n01001 10000 # j-q\n01010 01111 # k-p\n01011 01110 # l-o\n01100 01101 # m-n\n01101 01100 # n-m\n01110 01011 # o-l\n01111 01010 # p-k\n10000 01001 # q-j\n10001 01000 # r-i\n10010 00111 # s-h\n10011 00110 # t-g\n10100 00101 # u-f\n10101 00100 # v-e\n10110 00011 # w-d\n10111 00010 # x-c\n11000 00001 # y-b\n11001 00000 # z-a")) pla_2 (
    .in(bit_extender_8_out), .out(out_30));
  Bit_Extender #(.in_width(7), .out_width(5), .\type ("zero")) bit_extender_9 (
    .in(multiplexer_3_out), .out(bit_extender_9_out));
  PLA #(.in_width(5), .out_width(5), .\table ("00000 00000 # a-a\n00001 00001 # b-b\n00010 00010 # c-c\n00011 00011 # d-d\n00100 00100 # e-e\n00101 00101 # f-f\n00110 00110 # g-g\n00111 00111 # h-h\n01000 01000 # i-i\n01001 01001 # j-j\n01010 01010 # k-k\n01011 01011 # l-l\n01100 01100 # m-m\n01101 01101 # n-n\n01110 01110 # o-o\n01111 01111 # p-p\n10000 10000 # q-q\n10001 10001 # r-r\n10010 10010 # s-s\n10011 10011 # t-t\n10100 10100 # u-u\n10101 10101 # v-v\n10110 10110 # w-w\n10111 10111 # x-x\n11000 11000 # y-y\n11001 11001 # z-z")) pla_3 (
    .in(bit_extender_9_out), .out(out_32));
  Multiplexer #(.width(5)) multiplexer_4 (
    .in1(out_29), .out(multiplexer_4_out), .sel(priority_encoder_1_p19));  // open: in0
  PLA #(.in_width(5), .out_width(5), .\table ("00000 11001 # a-z\n00001 11000 # b-y\n00010 10111 # c-x\n00011 10110 # d-w\n00100 10101 # e-v\n00101 10100 # f-u\n00110 10011 # g-t\n00111 10010 # h-s\n01000 10001 # i-r\n01001 10000 # j-q\n01010 01111 # k-p\n01011 01110 # l-o\n01100 01101 # m-n\n01101 01100 # n-m\n01110 01011 # o-l\n01111 01010 # p-k\n10000 01001 # q-j\n10001 01000 # r-i\n10010 00111 # s-h\n10011 00110 # t-g\n10100 00101 # u-f\n10101 00100 # v-e\n10110 00011 # w-d\n10111 00010 # x-c\n11000 00001 # y-b\n11001 00000 # z-a")) pla_4 (
    .in(out_32), .out(pla_4_out));
  LED led_1 (.in(Q));
  LED led_2 (.in(A));
  Counter #(.max('h1f), .width(5)) counter_4 (
    .clr(and_4_out), .load(in_3), .up(in_5), .count(in_8), .clk(priority_encoder_1_p19), .Q(counter_4_q));  // open: D, carry
  and and_4 (and_4_out, not_7_out, counter_4_q[1], not_8_out, counter_4_q[3], counter_4_q[4]);
  Counter #(.max('h1f), .width(5)) counter_5 (
    .clr(and_5_out), .load(in_12), .up(in_14), .count(in_17), .clk(and_4_out), .Q(counter_5_q));  // open: D, carry
  and and_5 (and_5_out, not_9_out, counter_5_q[1], not_10_out, counter_5_q[3], counter_5_q[4]);
  Counter #(.max('h1f), .width(5)) counter_6 (
    .clr(and_6_out), .load(in_21), .up(in_23), .count(in_26), .clk(and_5_out), .Q(counter_6_q));  // open: D, carry
  and and_6 (and_6_out, not_11_out, counter_6_q[1], not_12_out, counter_6_q[3], counter_6_q[4]);
  LED led_3 (.in(W));
  LED led_4 (.in(E));
  LED led_5 (.in(S));
  LED led_6 (.in(Z));
  LED led_7 (.in(X));
  Decoder #(.select(5)) decoder_1 (
    .out0(A), .out1(B), .out2(C), .out3(D), .out4(E), .out5(F), .out6(G), .out7(H), .out8(I), .out9(J),
    .out10(K), .out11(L), .out12(M), .out13(N), .out14(O), .out15(P), .out16(Q), .out17(R), .out18(S),
    .out19(T), .out20(U), .out21(V), .out22(W), .out23(X), .out24(Y), .out25(Z), .sel(multiplexer_4_out));  // open: out26, out27, out28, out29, out30, out31, en
  not not_7 (not_7_out, counter_4_q[0]);
  not not_8 (not_8_out, counter_4_q[2]);
  not not_9 (not_9_out, counter_5_q[0]);
  not not_10 (not_10_out, counter_5_q[2]);
  not not_11 (not_11_out, counter_6_q[0]);
  not not_12 (not_12_out, counter_6_q[2]);
  LED led_8 (.in(R));
  LED led_9 (.in(D));
  LED led_10 (.in(F));
  LED led_11 (.in(C));
  LED led_12 (.in(T));
  LED led_13 (.in(G));
  LED led_14 (.in(V));
  PLA #(.in_width(5), .out_width(5), .\table ("00001 00000 # b-a\n00000 00001 # a-b\n00011 00010 # d-c\n00010 00011 # c-d\n00101 00100 # f-e\n00100 00101 # e-f\n00111 00110 # h-g\n00110 00111 # g-h\n01001 01000 # j-i\n01000 01001 # i-j\n01011 01010 # l-k\n01010 01011 # k-l\n01101 01100 # n-m\n01100 01101 # m-n\n01111 01110 # p-o\n01110 01111 # o-p\n10001 10000 # r-q\n10000 10001 # q-r\n10011 10010 # t-s\n10010 10011 # s-t\n10101 10100 # v-u\n10100 10101 # u-v\n10111 10110 # x-w\n10110 10111 # w-x\n11001 11000 # z-y\n11000 11001 # y-z")) pla_5 (
    .in(out_31), .out(pla_5_out));
  PLA #(.in_width(5), .out_width(5), .\table ("11001 00000 # z-a\n11000 00001 # y-b\n10111 00010 # x-c\n10110 00011 # w-d\n10101 00100 # v-e\n10100 00101 # u-f\n10011 00110 # t-g\n10010 00111 # s-h\n10001 01000 # r-i\n10000 01001 # q-j\n01111 01010 # p-k\n01110 01011 # o-l\n01101 01100 # n-m\n01100 01101 # m-n\n01011 01110 # l-o\n01010 01111 # k-p\n01001 10000 # j-q\n01000 10001 # i-r\n00111 10010 # h-s\n00110 10011 # g-t\n00101 10100 # f-u\n00100 10101 # e-v\n00011 10110 # d-w\n00010 10111 # c-x\n00001 11000 # b-y\n00000 11001 # a-z")) pla_6 (
    .in(out_33), .out(pla_6_out));
  PLA #(.in_width(5), .out_width(5), .\table ("00000 00000 # a-a\n00001 00001 # b-b\n00010 00010 # c-c\n00011 00011 # d-d\n00100 00100 # e-e\n00101 00101 # f-f\n00110 00110 # g-g\n00111 00111 # h-h\n01000 01000 # i-i\n01001 01001 # j-j\n01010 01010 # k-k\n01011 01011 # l-l\n01100 01100 # m-m\n01101 01101 # n-n\n01110 01110 # o-o\n01111 01111 # p-p\n10000 10000 # q-q\n10001 10001 # r-r\n10010 10010 # s-s\n10011 10011 # t-t\n10100 10100 # u-u\n10101 10101 # v-v\n10110 10110 # w-w\n10111 10111 # x-x\n11000 11000 # y-y\n11001 11001 # z-z")) pla_7 (
    .in(pla_4_out), .out(pla_7_out));
  LED led_15 (.in(Y));
  LED led_16 (.in(U));
  LED led_17 (.in(H));
  LED led_18 (.in(B));
  LED led_19 (.in(N));
  Comparator #(.mode("unsigned"), .width(5)) comparator_4 (
    .a(pla_5_out), .b(counter_4_q), .lt(comparator_4_lt));  // open: gt, eq
  Comparator #(.mode("unsigned"), .width(5)) comparator_5 (
    .a(pla_6_out), .b(counter_5_q), .lt(comparator_5_lt));  // open: gt, eq
  Comparator #(.mode("unsigned"), .width(5)) comparator_6 (
    .a(pla_7_out), .b(counter_6_q), .lt(comparator_6_lt));  // open: gt, eq
  LED led_20 (.in(I));
  LED led_21 (.in(J));
  LED led_22 (.in(K));
  LED led_23 (.in(M));
  Subtractor #(.width(5)) subtractor_4 (.a(pla_5_out), .b(counter_4_q), .out(subtractor_4_out));  // open: bin, bout
  Subtractor #(.width(5)) subtractor_5 (.a(pla_6_out), .b(counter_5_q), .out(subtractor_5_out));  // open: bin, bout
  Subtractor #(.width(5)) subtractor_6 (.a(pla_7_out), .b(counter_6_q), .out(subtractor_6_out));  // open: bin, bout
  LED led_24 (.in(O));
  LED led_25 (.in(L));
  Adder #(.width(5)) adder_4 (.a(in_1), .b(subtractor_4_out), .out(adder_4_out));  // open: cin, cout
  Adder #(.width(5)) adder_5 (.a(in_10), .b(subtractor_5_out), .out(adder_5_out));  // open: cin, cout
  Adder #(.width(5)) adder_6 (.a(in_19), .b(subtractor_6_out), .out(adder_6_out));  // open: cin, cout
  LED led_26 (.in(P));
  Multiplexer #(.width(5)) multiplexer_5 (
    .in0(subtractor_4_out), .in1(adder_4_out), .out(out_29), .sel(comparator_4_lt));
  Multiplexer #(.width(5)) multiplexer_6 (
    .in0(subtractor_5_out), .in1(adder_5_out), .out(out_31), .sel(comparator_5_lt));
  Multiplexer #(.width(5)) multiplexer_7 (
    .in0(subtractor_6_out), .in1(adder_6_out), .out(out_33), .sel(comparator_6_lt));

  // Notes on the sheet:
  //   KeyBoard
  //   PlugBoard
  //   Rotor1
  //   Rotor2
  //   Rotor3
  //   Reflector
  //   LightBulb
  //   Inverse PlugBoard
  //   Inverse Rotor1
  //   Inverse Rotor2
  //   Inverse Rotor3
endmodule
