// Logisim project Circuit 3. Register.circ as structural Verilog: 1 circuit, main circuit main
module main (
  input  [7:0] D_in,
  input  WH,
  input  WL,
  input  CLK,
  output [7:0] D_out
);

  wire controlled_buffer_1_out, controlled_buffer_2_out, controlled_buffer_3_out, controlled_buffer_4_out,
       controlled_buffer_5_out, controlled_buffer_6_out, controlled_buffer_7_out, controlled_buffer_8_out;

  assign controlled_buffer_1_out = WH ? D_in[7] : 1'bz;  // Controlled_Buffer controlled_buffer_1
  D_Flip_Flop d_ff_1 (.D(controlled_buffer_1_out), .clk(CLK), .Q(D_out[7]));  // open: Qn, preset, reset
  assign controlled_buffer_2_out = WH ? D_in[6] : 1'bz;  // Controlled_Buffer controlled_buffer_2
  D_Flip_Flop d_ff_2 (.D(controlled_buffer_2_out), .clk(CLK), .Q(D_out[6]));  // open: Qn, preset, reset
  assign controlled_buffer_3_out = WH ? D_in[5] : 1'bz;  // Controlled_Buffer controlled_buffer_3
  D_Flip_Flop d_ff_3 (.D(controlled_buffer_3_out), .clk(CLK), .Q(D_out[5]));  // open: Qn, preset, reset
  assign controlled_buffer_4_out = WH ? D_in[4] : 1'bz;  // Controlled_Buffer controlled_buffer_4
  D_Flip_Flop d_ff_4 (.D(controlled_buffer_4_out), .clk(CLK), .Q(D_out[4]));  // open: Qn, preset, reset
  assign controlled_buffer_5_out = WL ? D_in[3] : 1'bz;  // Controlled_Buffer controlled_buffer_5
  D_Flip_Flop d_ff_5 (.D(controlled_buffer_5_out), .clk(CLK), .Q(D_out[3]));  // open: Qn, preset, reset
  assign controlled_buffer_6_out = WL ? D_in[2] : 1'bz;  // Controlled_Buffer controlled_buffer_6
  D_Flip_Flop d_ff_6 (.D(controlled_buffer_6_out), .clk(CLK), .Q(D_out[2]));  // open: Qn, preset, reset
  assign controlled_buffer_7_out = WL ? D_in[1] : 1'bz;  // Controlled_Buffer controlled_buffer_7
  D_Flip_Flop d_ff_7 (.D(controlled_buffer_7_out), .clk(CLK), .Q(D_out[1]));  // open: Qn, preset, reset
  assign controlled_buffer_8_out = WL ? D_in[0] : 1'bz;  // Controlled_Buffer controlled_buffer_8
  D_Flip_Flop d_ff_8 (.D(controlled_buffer_8_out), .clk(CLK), .Q(D_out[0]));  // open: Qn, preset, reset
endmodule
