// Logisim project Circuit 9. Read Only Memory.circ as structural Verilog: 1 circuit, main circuit main
module main (
  input  A,
  input  B,
  input  C_in
);

  wire [1:0] pla_1_out;

  PLA #(.in_width(3), .\table ("000 00\n001 01\n010 01\n011 10\n100 01\n101 10\n110 10\n111 11")) pla_1 (
    .in({C_in, B, A}), .out(pla_1_out));
  LED led_1 (.in(pla_1_out[1]));
  LED led_2 (.in(pla_1_out[0]));

  // Notes on the sheet:
  //   Full_Adder
  //   C_out
  //   S
endmodule
